# Fritzing sketch LED (saved by Fritzing 0.9.3b)
breadboards: 1

parts:
  Componente1 = Arduino Uno (Rev3)
  LED1 = smd LED [color="Red (633nm)" package="1206 [SMD]"]
  R1 = Resistor [tolerance=±5% resistance=220 package="0603 [SMD]"]

nets:
  N1: Componente1.D13/SCK, LED1.anode, R1.Pin_0, R1.Pin_1
  N2: Componente1.GND, LED1.cathode

// code stored in the sketch: Aula1.ino

int iPin = 13;
int iDelay = 25;

void setup() {

  Serial.begin(9600);
  pinMode(iPin, OUTPUT);
}

void loop() {

  digitalWrite(iPin, HIGH);
  delay(iDelay);
  digitalWrite(iPin, LOW);
  delay(iDelay);
}
