# Fritzing sketch botao (saved by Fritzing 0.9.3b)
breadboards: 1

parts:
  S1 = Pushbutton [package="[THT]"]
  S2 = Pushbutton [package="[THT]"]
  LED1 = LED - 5mm [color="Red (633nm)" package="5 mm [THT]"]
  Componente1 = Arduino Uno (Rev3) - ICSP
  R1 = Resistor [tolerance=±5% resistance=330 package="2010 [SMD]"]
  R2 = Resistor [tolerance=±5% resistance=10k package="2010 [SMD]"]
  R3 = Resistor [tolerance=±5% resistance=10k package="2010 [SMD]"]

nets:
  N1: S1.Pin_1, S1.Pin_2, S2.Pin_1, S2.Pin_2, Componente1.5V
  N2: S1.Pin_3, S1.Pin_4, Componente1.D6_PWM, R2.Pin_1
  N3: S2.Pin_3, S2.Pin_4, Componente1.D7, R3.Pin_1
  N4: LED1.cathode, Componente1.GND, R2.Pin_0, R3.Pin_0
  N5: LED1.anode, Componente1.D13/SCK, R1.Pin_0, R1.Pin_1
