# Fritzing sketch luz (saved by Fritzing 0.9.3b)
breadboards: 1

parts:
  LED1 = LED - 5mm [color="Red (633nm)" package="5 mm [THT]"]
  Componente1 = Arduino Uno (Rev3) - ICSP
  R1 = Resistor [tolerance=±5% resistance=330 package="2010 [SMD]"]

nets:
  N1: LED1.cathode, Componente1.GND
  N2: LED1.anode, Componente1.D13/SCK, R1.Pin_0, R1.Pin_1
